// Logisim project SC2.circ as structural Verilog: 3 circuits, main circuit main
module main (
  input  Reset,
  input  AM_PM,
  input  AlarmEnable,
  input  LoadAlarm,
  input  LoadTime,
  input  [5:0] D_hours,
  input  [5:0] D_Mins,
  input  [5:0] D_secs,
  output [3:0] H_T_O,
  output [3:0] H_O_O,
  output [3:0] M_T_O,
  output [3:0] M_O_O,
  output [3:0] S_T_O,
  output [3:0] S_O_O
);

  wire and_1_out, and_2_out, and_3_out, comparator_1_eq, comparator_2_eq, comparator_3_eq, comparator_4_eq,
       comparator_5_eq, comparator_6_eq, comparator_7_eq, comparator_8_eq, comparator_9_eq, comparator_10_eq,
       comparator_11_eq, comparator_12_eq, Hour_seg2_a, Hour_seg2_b, Hour_seg2_c, Hour_seg2_d, Hour_seg2_e,
       Hour_seg2_f, Hour_seg2_g, Hour_seg_a, Hour_seg_b, Hour_seg_c, Hour_seg_d, Hour_seg_e, Hour_seg_f,
       Hour_seg_g, Min_seg2_a, Min_seg2_b, Min_seg2_c, Min_seg2_d, Min_seg2_e, Min_seg2_f, Min_seg2_g,
       Min_seg_a, Min_seg_b, Min_seg_c, Min_seg_d, Min_seg_e, Min_seg_f, Min_seg_g, not_1_out, or_1_out,
       or_2_out, or_3_out, or_4_out, or_5_out, or_6_out, or_7_out, or_8_out, or_9_out, or_10_out, or_11_out,
       or_12_out, or_13_out, or_14_out, or_15_out, register_1_q, register_2_q, Sec_seg2_a, Sec_seg2_b,
       Sec_seg2_c, Sec_seg2_d, Sec_seg2_e, Sec_seg2_f, Sec_seg2_g, Sec_seg_a, Sec_seg_b, Sec_seg_c,
       Sec_seg_d, Sec_seg_e, Sec_seg_f, Sec_seg_g;
  wire [1:0] d_ff_1_qn, priority_encoder_1_out, register_9_q;
  wire [3:0] counter_1_q, counter_2_q, counter_3_q, counter_4_q, counter_5_q, counter_6_q, Hour_c_o3,
       Hour_c_t3, Min_c_o3, Min_c_t3, register_3_q, register_4_q, register_5_q, register_6_q, register_7_q,
       register_8_q, Sec_c_o3, Sec_c_t3;
  wire [3:3] Clock_1sec_out;
  wire [6:0] multiplexer_7_out;

  Clock Clock_1sec (.out(Clock_1sec_out[3]));
  Counter #(.max('hf), .width(4)) counter_1 (
    .clr(or_2_out), .load(LoadTime), .up(1'b1), .count(1'b1), .clk(or_1_out), .D(Sec_c_t3), .Q(counter_1_q));  // open: carry
  or or_1 (or_1_out, Clock_1sec_out[3], LoadTime);
  or or_2 (or_2_out, or_13_out, comparator_1_eq);
  Counter #(.max('hf), .width(4)) counter_2 (
    .clr(or_4_out), .load(LoadTime), .up(1'b1), .count(1'b1), .clk(or_3_out), .D(Sec_c_o3), .Q(counter_2_q));  // open: carry
  or or_3 (or_3_out, comparator_1_eq, LoadTime);
  or or_4 (or_4_out, or_13_out, comparator_2_eq);
  Comparator #(.width(4)) comparator_1 (.a(counter_1_q), .b(4'b1010), .eq(comparator_1_eq));  // open: gt, lt
  Comparator #(.width(4)) comparator_2 (.a(counter_2_q), .b(4'b0110), .eq(comparator_2_eq));  // open: gt, lt
  Bin_to_BCD Sec_c (
    .D5(D_secs[0]), .D4(D_secs[1]), .D3(D_secs[2]), .D2(D_secs[3]), .D1(D_secs[4]), .D0(D_secs[5]),
    .T0(Sec_c_t3[3]), .T1(Sec_c_t3[2]), .T2(Sec_c_t3[1]), .T3(Sec_c_t3[0]), .O0(Sec_c_o3[3]),
    .O1(Sec_c_o3[2]), .O2(Sec_c_o3[1]), .O3(Sec_c_o3[0]));
  Counter #(.max('hf), .width(4)) counter_3 (
    .clr(or_6_out), .load(LoadTime), .up(1'b1), .count(1'b1), .clk(or_5_out), .D(Min_c_t3), .Q(counter_3_q));  // open: carry
  or or_5 (or_5_out, comparator_2_eq, LoadTime);
  or or_6 (or_6_out, or_13_out, comparator_3_eq);
  Counter #(.max('hf), .width(4)) counter_4 (
    .clr(or_8_out), .load(LoadTime), .up(1'b1), .count(1'b1), .clk(or_7_out), .D(Min_c_o3), .Q(counter_4_q));  // open: carry
  or or_7 (or_7_out, comparator_3_eq, LoadTime);
  or or_8 (or_8_out, or_13_out, comparator_4_eq);
  Bin_to_BCD Min_c (
    .D5(D_Mins[0]), .D4(D_Mins[1]), .D3(D_Mins[2]), .D2(D_Mins[3]), .D1(D_Mins[4]), .D0(D_Mins[5]),
    .T0(Min_c_t3[3]), .T1(Min_c_t3[2]), .T2(Min_c_t3[1]), .T3(Min_c_t3[0]), .O0(Min_c_o3[3]),
    .O1(Min_c_o3[2]), .O2(Min_c_o3[1]), .O3(Min_c_o3[0]));
  Comparator #(.width(4)) comparator_3 (.a(counter_3_q), .b(4'b1010), .eq(comparator_3_eq));  // open: gt, lt
  Comparator #(.width(4)) comparator_4 (.a(counter_4_q), .b(4'b0110), .eq(comparator_4_eq));  // open: gt, lt
  Bin_to_BCD Hour_c (
    .D5(D_hours[0]), .D4(D_hours[1]), .D3(D_hours[2]), .D2(D_hours[3]), .D1(D_hours[4]), .D0(D_hours[5]),
    .T0(Hour_c_t3[3]), .T1(Hour_c_t3[2]), .T2(Hour_c_t3[1]), .T3(Hour_c_t3[0]), .O0(Hour_c_o3[3]),
    .O1(Hour_c_o3[2]), .O2(Hour_c_o3[1]), .O3(Hour_c_o3[0]));
  Counter #(.max('hf), .width(4)) counter_5 (
    .clr(or_10_out), .load(LoadTime), .up(1'b1), .count(1'b1), .clk(or_9_out), .D(Hour_c_t3), .Q(counter_5_q));  // open: carry
  or or_9 (or_9_out, comparator_4_eq, LoadTime);
  or or_10 (or_10_out, or_13_out, comparator_5_eq);
  Counter #(.max('hf), .width(4)) counter_6 (
    .clr(or_12_out), .load(LoadTime), .up(1'b1), .count(1'b1), .clk(or_11_out), .D(Hour_c_o3), .Q(counter_6_q));  // open: carry
  or or_11 (or_11_out, comparator_5_eq, LoadTime);
  or or_12 (or_12_out, or_13_out, comparator_6_eq);
  Comparator #(.width(4)) comparator_5 (.a(counter_5_q), .b(4'b1010), .eq(comparator_5_eq));  // open: gt, lt
  Comparator #(.width(4)) comparator_6 (.a(counter_6_q), .b(4'b0010), .eq(comparator_6_eq));  // open: gt, lt
  Register #(.width(1)) register_1 (
    .D(comparator_1_eq), .en(AlarmEnable), .clk(Clock_1sec_out[3]), .Q(register_1_q), .clr(comparator_3_eq));
  Comparator #(.width(4)) comparator_7 (.a(4'b0010), .b(counter_5_q), .eq(comparator_7_eq));  // open: gt, lt
  Comparator #(.width(4)) comparator_8 (.a(counter_6_q), .b(4'b0001), .eq(comparator_8_eq));  // open: gt, lt
  and and_1 (and_1_out, AM_PM, LoadTime);
  or or_13 (or_13_out, and_2_out, Reset);
  Priority_Encoder #(.select(2)) priority_encoder_1 (
    .in0(1'b1), .in1(LoadTime), .in2(LoadAlarm), .in3(register_2_q), .out(priority_encoder_1_out));  // open: gs, en_out, en_in
  and and_2 (and_2_out, comparator_7_eq, comparator_8_eq);
  BCD_to_7seg Hour_seg (
    .D3(H_T_O[3]), .D2(H_T_O[2]), .D1(H_T_O[1]), .D0(H_T_O[0]), .A(Hour_seg_a), .B(Hour_seg_b),
    .C(Hour_seg_c), .D(Hour_seg_d), .E(Hour_seg_e), .F(Hour_seg_f), .G(Hour_seg_g));
  BCD_to_7seg Hour_seg2 (
    .D3(H_O_O[3]), .D2(H_O_O[2]), .D1(H_O_O[1]), .D0(H_O_O[0]), .A(Hour_seg2_a), .B(Hour_seg2_b),
    .C(Hour_seg2_c), .D(Hour_seg2_d), .E(Hour_seg2_e), .F(Hour_seg2_f), .G(Hour_seg2_g));
  BCD_to_7seg Min_seg (
    .D3(M_T_O[3]), .D2(M_T_O[2]), .D1(M_T_O[1]), .D0(M_T_O[0]), .A(Min_seg_a), .B(Min_seg_b), .C(Min_seg_c),
    .D(Min_seg_d), .E(Min_seg_e), .F(Min_seg_f), .G(Min_seg_g));
  BCD_to_7seg Min_seg2 (
    .D3(M_O_O[3]), .D2(M_O_O[2]), .D1(M_O_O[1]), .D0(M_O_O[0]), .A(Min_seg2_a), .B(Min_seg2_b),
    .C(Min_seg2_c), .D(Min_seg2_d), .E(Min_seg2_e), .F(Min_seg2_f), .G(Min_seg2_g));
  BCD_to_7seg Sec_seg (
    .D3(S_T_O[3]), .D2(S_T_O[2]), .D1(S_T_O[1]), .D0(S_T_O[0]), .A(Sec_seg_a), .B(Sec_seg_b), .C(Sec_seg_c),
    .D(Sec_seg_d), .E(Sec_seg_e), .F(Sec_seg_f), .G(Sec_seg_g));
  BCD_to_7seg Sec_seg2 (
    .D3(S_O_O[3]), .D2(S_O_O[2]), .D1(S_O_O[1]), .D0(S_O_O[0]), .A(Sec_seg2_a), .B(Sec_seg2_b),
    .C(Sec_seg2_c), .D(Sec_seg2_d), .E(Sec_seg2_e), .F(Sec_seg2_f), .G(Sec_seg2_g));
  Register #(.width(1)) register_2 (
    .D(and_3_out), .en(AlarmEnable), .clk(Clock_1sec_out[3]), .Q(register_2_q), .clr(or_15_out));
  or or_14 (or_14_out, and_1_out, and_2_out);
  _7_Segment_Display HT_O (
    .g(Hour_seg_g), .f(Hour_seg_f), .a(Hour_seg_a), .b(Hour_seg_b), .e(Hour_seg_e), .d(Hour_seg_d),
    .c(Hour_seg_c), .dp(1'b0));
  or or_15 (or_15_out, register_1_q, Reset);
  _7_Segment_Display HO_O (
    .g(Hour_seg2_g), .f(Hour_seg2_f), .a(Hour_seg2_a), .b(Hour_seg2_b), .e(Hour_seg2_e), .d(Hour_seg2_d),
    .c(Hour_seg2_c), .dp(Clock_1sec_out[3]));
  Comparator #(.width(4)) comparator_9 (.a(counter_3_q), .b(register_5_q), .eq(comparator_9_eq));  // open: gt, lt
  Comparator #(.width(4)) comparator_10 (.a(counter_4_q), .b(register_6_q), .eq(comparator_10_eq));  // open: gt, lt
  Comparator #(.width(4)) comparator_11 (.a(counter_5_q), .b(register_7_q), .eq(comparator_11_eq));  // open: gt, lt
  Comparator #(.width(4)) comparator_12 (.a(counter_6_q), .b(register_8_q), .eq(comparator_12_eq));  // open: gt, lt
  Register #(.width(4)) register_3 (
    .D(Sec_c_t3), .en(LoadAlarm), .clk(Clock_1sec_out[3]), .Q(register_3_q));  // open: clr
  _7_Segment_Display MT_O (
    .g(Min_seg_g), .f(Min_seg_f), .a(Min_seg_a), .b(Min_seg_b), .e(Min_seg_e), .d(Min_seg_d), .c(Min_seg_c),
    .dp(1'b0));
  and and_3 (and_3_out, comparator_9_eq, comparator_10_eq, comparator_11_eq, comparator_12_eq);
  Register #(.width(4)) register_4 (
    .D(Sec_c_o3), .en(LoadAlarm), .clk(Clock_1sec_out[3]), .Q(register_4_q));  // open: clr
  Multiplexer #(.select(2), .width(4)) multiplexer_1 (
    .in0(counter_1_q), .in1(Sec_c_t3), .in2(register_3_q), .in3({4{Clock_1sec_out[3]}}), .out(S_O_O),
    .sel(priority_encoder_1_out));
  Register #(.width(4)) register_5 (
    .D(Min_c_t3), .en(LoadAlarm), .clk(Clock_1sec_out[3]), .Q(register_5_q));  // open: clr
  _7_Segment_Display MO_O (
    .g(Min_seg2_g), .f(Min_seg2_f), .a(Min_seg2_a), .b(Min_seg2_b), .e(Min_seg2_e), .d(Min_seg2_d),
    .c(Min_seg2_c), .dp(Clock_1sec_out[3]));
  Multiplexer #(.select(2), .width(4)) multiplexer_2 (
    .in0(counter_2_q), .in1(Sec_c_o3), .in2(register_4_q), .in3({4{Clock_1sec_out[3]}}), .out(S_T_O),
    .sel(priority_encoder_1_out));
  Multiplexer #(.select(2), .width(4)) multiplexer_3 (
    .in0(counter_3_q), .in1(Min_c_t3), .in2(register_5_q), .in3({4{Clock_1sec_out[3]}}), .out(M_O_O),
    .sel(priority_encoder_1_out));
  Register #(.width(4)) register_6 (
    .D(Min_c_o3), .en(LoadAlarm), .clk(Clock_1sec_out[3]), .Q(register_6_q));  // open: clr
  _7_Segment_Display ST_O (
    .g(Sec_seg_g), .f(Sec_seg_f), .a(Sec_seg_a), .b(Sec_seg_b), .e(Sec_seg_e), .d(Sec_seg_d), .c(Sec_seg_c),
    .dp(1'b0));
  Multiplexer #(.select(2), .width(4)) multiplexer_4 (
    .in0(counter_4_q), .in1(Min_c_o3), .in2(register_6_q), .in3({4{Clock_1sec_out[3]}}), .out(M_T_O),
    .sel(priority_encoder_1_out));
  Register #(.width(4)) register_7 (
    .D(Hour_c_t3), .en(LoadAlarm), .clk(Clock_1sec_out[3]), .Q(register_7_q));  // open: clr
  Multiplexer #(.select(2), .width(4)) multiplexer_5 (
    .in0(counter_5_q), .in1(Hour_c_t3), .in2(register_7_q), .in3({4{Clock_1sec_out[3]}}), .out(H_O_O),
    .sel(priority_encoder_1_out));
  Register #(.width(4)) register_8 (
    .D(Hour_c_o3), .en(LoadAlarm), .clk(Clock_1sec_out[3]), .Q(register_8_q));  // open: clr
  _7_Segment_Display SO_O (
    .g(Sec_seg2_g), .f(Sec_seg2_f), .a(Sec_seg2_a), .b(Sec_seg2_b), .e(Sec_seg2_e), .d(Sec_seg2_d),
    .c(Sec_seg2_c), .dp(1'b0));
  Register #(.width(2)) register_9 (.D(d_ff_1_qn), .en(1'b1), .clk(Clock_1sec_out[3]), .Q(register_9_q), .clr(Reset));
  Multiplexer #(.select(2), .width(4)) multiplexer_6 (
    .in0(counter_6_q), .in1(Hour_c_o3), .in2(register_8_q), .in3({4{Clock_1sec_out[3]}}), .out(H_T_O),
    .sel(priority_encoder_1_out));
  _7_Segment_Display Status (
    .g(multiplexer_7_out[0]), .f(multiplexer_7_out[1]), .a(multiplexer_7_out[6]), .b(multiplexer_7_out[5]),
    .e(multiplexer_7_out[2]), .d(multiplexer_7_out[3]), .c(multiplexer_7_out[4]), .dp(1'b0));
  Multiplexer #(.select(2), .width(7)) multiplexer_7 (
    .in0({7{1'b0}}), .in1(7'b1110111), .in2(7'b1100111), .in3(7'b0001110), .out(multiplexer_7_out),
    .sel(register_9_q));
  not not_1 (not_1_out, d_ff_1_qn[1]);
  D_Flip_Flop d_ff_1 (
    .D(not_1_out), .clk(or_14_out), .Q(d_ff_1_qn[1]), .Qn(d_ff_1_qn[0]), .reset(Reset));  // open: preset

  // Notes on the sheet:
  //   Counter block
  //   Output Block
endmodule

module Bin_to_BCD (
  input  D5,
  input  D4,
  input  D3,
  input  D2,
  input  D1,
  input  D0,
  output T0,
  output T1,
  output T2,
  output T3,
  output O0,
  output O1,
  output O2,
  output O3
);

  wire and_1_out, and_2_out, and_3_out, and_4_out, and_5_out, and_6_out, and_7_out, and_8_out, and_9_out,
       and_10_out, and_11_out, and_12_out, and_13_out, and_14_out, and_15_out, and_16_out, and_17_out,
       and_18_out, and_19_out, and_20_out, and_21_out, and_22_out, and_23_out, and_24_out, and_25_out,
       and_26_out, and_27_out, and_28_out, and_29_out, and_30_out, and_31_out, and_32_out, and_33_out,
       and_34_out, and_35_out, and_36_out, and_37_out, and_38_out, and_39_out, and_40_out, not_1_out,
       not_2_out, not_3_out, not_4_out, not_5_out;

  not not_1 (not_1_out, D5);
  not not_2 (not_2_out, D4);
  not not_3 (not_3_out, D3);
  not not_4 (not_4_out, D2);
  not not_5 (not_5_out, D1);
  and and_1 (and_1_out, D5, D3);
  and and_2 (and_2_out, D5, D4);
  and and_3 (and_3_out, D5, not_2_out, not_3_out);
  and and_4 (and_4_out, not_1_out, D4, D2);
  and and_5 (and_5_out, not_1_out, D4, D3);
  and and_6 (and_6_out, D4, D3, D2);
  and and_7 (and_7_out, not_1_out, not_2_out, D3, D1);
  and and_8 (and_8_out, not_1_out, not_2_out, D3, D2);
  and and_9 (and_9_out, not_1_out, D4, not_3_out, not_4_out);
  and and_10 (and_10_out, not_1_out, D3, D2, D1);
  and and_11 (and_11_out, D5, not_2_out, not_3_out);
  and and_12 (and_12_out, D5, not_3_out, D2);
  and and_13 (and_13_out, D5, D4, D3, not_4_out);
  and and_14 (and_14_out, D4, not_3_out, not_4_out, D1);
  and and_15 (and_15_out, D5, D4, not_3_out, not_4_out, not_5_out);
  and and_16 (and_16_out, not_1_out, D4, not_3_out, not_4_out, D1);
  and and_17 (and_17_out, D5, not_2_out, not_3_out, D2, D1);
  and and_18 (and_18_out, not_1_out, not_2_out, D3, not_4_out, not_5_out);
  and and_19 (and_19_out, D5, D4, D3, not_4_out, D1);
  and and_20 (and_20_out, not_1_out, D4, D3, D2, not_5_out);
  and and_21 (and_21_out, D5, not_2_out, not_3_out, not_4_out, D1);
  and and_22 (and_22_out, not_1_out, D4, not_4_out, not_5_out);
  and and_23 (and_23_out, D5, D4, not_3_out, D2, D1);
  and and_24 (and_24_out, D4, D3, not_4_out, not_5_out);
  and and_25 (and_25_out, not_1_out, D4, D3, not_4_out);
  and and_26 (and_26_out, not_2_out, not_3_out, D2, not_5_out);
  and and_27 (and_27_out, not_1_out, not_2_out, not_3_out, D2);
  and and_28 (and_28_out, D5, not_2_out, D2, not_5_out);
  and and_29 (and_29_out, not_1_out, not_2_out, D2, D1);
  and and_30 (and_30_out, D5, not_2_out, D3, D2);
  and and_31 (and_31_out, not_1_out, not_2_out, not_3_out, D1);
  and and_32 (and_32_out, not_1_out, not_2_out, D3, D2, not_5_out);
  and and_33 (and_33_out, not_1_out, D4, not_3_out, not_4_out, not_5_out);
  and and_34 (and_34_out, not_1_out, not_3_out, D2, D1);
  and and_35 (and_35_out, not_1_out, D4, D3, not_4_out, D1);
  and and_36 (and_36_out, D5, not_2_out, not_3_out, not_5_out);
  and and_37 (and_37_out, D5, not_2_out, D3, D1);
  and and_38 (and_38_out, D5, not_3_out, D2, not_5_out);
  and and_39 (and_39_out, D5, D4, D3, not_4_out, not_5_out);
  and and_40 (and_40_out, D5, D3, D2, D1);
  or or_1 (O1, and_1_out, and_2_out);
  or or_2 (O2, and_3_out, and_4_out, and_5_out, and_6_out);
  or or_3 (O3, and_7_out, and_8_out, and_9_out, and_10_out, and_11_out, and_12_out, and_13_out, and_14_out);
  or or_4 (T0, and_15_out, and_16_out, and_17_out, and_18_out, and_19_out, and_20_out);
  or or_5 (T1, and_21_out, and_22_out, and_23_out, and_24_out, and_25_out, and_26_out, and_27_out, and_28_out, and_29_out, and_30_out);
  or or_6 (T2, and_31_out, and_32_out, and_33_out, and_34_out, and_35_out, and_36_out, and_37_out, and_38_out, and_39_out, and_40_out);

  assign O0 = 1'b0;
  assign T3 = D0;
endmodule

module BCD_to_7seg (
  input  D3,
  input  D2,
  input  D1,
  input  D0,
  output A,
  output B,
  output C,
  output D,
  output E,
  output F,
  output G
);

  wire and_1_out, and_2_out, and_3_out, and_4_out, and_5_out, and_6_out, and_7_out, and_8_out, and_9_out,
       and_10_out, and_11_out, and_12_out, and_13_out, and_14_out, and_15_out, and_16_out, not_1_out,
       not_2_out, not_3_out;

  not not_1 (not_1_out, D2);
  not not_2 (not_2_out, D1);
  not not_3 (not_3_out, D0);
  and and_1 (and_1_out, not_1_out, not_3_out);
  and and_2 (and_2_out, D2, D0);
  and and_3 (and_3_out, not_2_out, not_3_out);
  and and_4 (and_4_out, D1, D0);
  or or_1 (C, not_2_out, D0, D2);
  and and_5 (and_5_out, not_1_out, not_3_out);
  and and_6 (and_6_out, not_1_out, D1);
  and and_7 (and_7_out, D2, not_2_out, D0);
  and and_8 (and_8_out, D1, not_3_out);
  and and_9 (and_9_out, not_1_out, not_3_out);
  and and_10 (and_10_out, D1, not_3_out);
  and and_11 (and_11_out, not_2_out, not_3_out);
  and and_12 (and_12_out, D2, not_2_out);
  and and_13 (and_13_out, D2, not_3_out);
  and and_14 (and_14_out, not_1_out, D1);
  and and_15 (and_15_out, D2, not_2_out);
  and and_16 (and_16_out, D1, not_3_out);
  or or_2 (A, and_1_out, D1, and_2_out, D3);
  or or_3 (B, not_1_out, and_3_out, and_4_out);
  or or_4 (D, and_5_out, and_6_out, and_7_out, and_8_out, D3);
  or or_5 (E, and_9_out, and_10_out);
  or or_6 (F, and_11_out, and_12_out, and_13_out, D3);
  or or_7 (G, and_14_out, and_15_out, D3, and_16_out);
endmodule
